# Fritzing sketch Untitled Sketch (saved by Fritzing 0.9.6b)
breadboards: 1

parts:
  WeMos_D1_Mini1 = WeMos D1 Mini
  R1 = Resistor [tolerance=±5% power=0.25 resistance=220 package=THT]
  S1 = Pushbutton [package="[THT]"]
  S2 = Pushbutton [package="[THT]"]
  R2 = Resistor [tolerance=±5% power=0.25 resistance=220 package=THT]
  LED1 = LED - 5mm [color="Red (633nm)" current=0.030 package="5 mm [THT]"]
  LED2 = LED - 5mm [color="Red (633nm)" current=0.030 package="5 mm [THT]"]
  J1 = Basic Servo

nets:
  5V: WeMos_D1_Mini1.5V, J1.vcc
  N1: WeMos_D1_Mini1.D5, J1.pulse
  N2: WeMos_D1_Mini1.G, R1.Pin_1, R2.Pin_1, J1.gnd
  N3: R1.Pin_0, LED1.cathode
  N4: S1.Pin_1, S1.Pin_2, S2.Pin_1, S2.Pin_2
  N5: S1.Pin_3, S1.Pin_4
  N6: S2.Pin_3, S2.Pin_4
  N7: R2.Pin_0, LED2.cathode

custom parts:
  WeMos D1 Mini: The D1 mini is a mini wifi board based on ESP-8266EX.
